# Fritzing sketch Version_1 (saved by Fritzing 0.9.3b)
breadboards: 1

parts:
  Часть1 = Arduino Nano (Rev3.0)  # not connected
  Часть3 = Adafruit BME280  # not connected
  Часть4 = MQ-3 breakout  # not connected
  Component1 = RS485-Modul-Shield

nets:
  N1: Component1.RE, Component1.DE

custom parts:
  Adafruit BME280: Bosch has stepped up their game with their new BME280 sensor, an environmental sensor with temperature, barometric pressure and humidity! This sensor is great for all sorts of weather/environmental sensing and can even be used in both I2C and SPI! This precision sensor from Bosch is the best low-cost sensing solution for measuring humidity with ±3% accuracy, barometric pressure with ±1 hPa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
  MQ-3 breakout: Alcohol sensor is capable of detecting alcohol (ethanol) particles on itself and gives the information in digital form back to us to manipulate with it. SKU:101251 • Voltage: 5V DC • Power: max 750mW • Measurement range: 0.04-4mg/L
  RS485-Modul-Shield: Commercially available RS485 to RS232 TTL Module
