# Fritzing sketch arduino_2_rs485 (saved by Fritzing 0.9.3b)

parts:
  Часть1 = Arduino Nano (Rev3.0)
  Grove1 = Grove 4 Digit Display  # not connected
  Component1 = RS485-Modul-Shield
  LED1 = LED - 5mm [color="Red (633nm)" package="5 mm [THT]"]  # not connected
  R1 = Resistor [tolerance=±5% resistance=220 package=THT]

nets:
  N1: Часть1.D0/RX, Component1.RO
  N2: Часть1.D5, R1.Pin_0

custom parts:
  RS485-Modul-Shield: Commercially available RS485 to RS232 TTL Module
